// Logisim project milestoneFinalEDittionn.circ as structural Verilog: 3 circuits, main circuit main
module main (
  output out_1
);

  wire CLEAR_SC, clock_1_out, d_ff_1_q, I, INC_PC, INC_SC, LD_AC, LD_AR, LD_DR, LD_IR, LD_PC, MEMORY_READ,
       MEMORY_WRITE;
  wire [2:0] ALU_SELECTION, BUS_SELECTION, OPCode;
  wire [3:0] SC;
  wire [6:0] AR_q, bit_extender_1_out;
  wire [11:0] Address;
  wire [15:0] AC, alu_1_ac_output, bit_extender_2_out, DR_q, multiplexer_1_out, PC_q, ram_1_data, TR_q;

  D_Flip_Flop d_ff_1 (.clk(clock_1_out), .D(CLEAR_SC), .Q(d_ff_1_q));  // open: Qn, preset, en, reset
  Bit_Extender #(.in_width(16), .out_width(7)) bit_extender_1 (.in(multiplexer_1_out), .out(bit_extender_1_out));
  Clock clock_1 (.out(clock_1_out));
  Control_Unit control_unit_1 (
    .I_bit(I), .OPCode(OPCode), .SC(SC), .Address_part(Address), .AC(AC), .LD_AR(LD_AR), .LD_PC(LD_PC),
    .LD_DR(LD_DR), .LD_IR(LD_IR), .memory_write(MEMORY_WRITE), .LD_AC(LD_AC), .memory_read(MEMORY_READ),
    .Bus_selection(BUS_SELECTION), .INC_PC(INC_PC), .ALU_Selection(ALU_SELECTION), .CLEAR_SC(CLEAR_SC),
    .INC_SC(INC_SC));
  Register #(.width(7)) AR (.D(bit_extender_1_out), .en(LD_AR), .Q(AR_q), .clk(clock_1_out));  // open: clr
  Register #(.width(16)) TR (.D(multiplexer_1_out), .Q(TR_q), .clk(clock_1_out));  // open: en, clr
  Register #(.width(16)) DR (.D(multiplexer_1_out), .en(LD_DR), .Q(DR_q), .clk(clock_1_out));  // open: clr
  Register #(.width(16)) u_AC (.D(alu_1_ac_output), .en(LD_AC), .Q(AC), .clk(clock_1_out));  // open: clr
  Counter #(.width(16), .max('hffff)) PC (
    .load(LD_PC), .D(multiplexer_1_out), .count(INC_PC), .Q(PC_q), .clk(clock_1_out));  // open: carry, clr
  Register #(.width(16)) IR (
    .D(multiplexer_1_out), .en(LD_IR), .Q({I, OPCode, Address}), .clk(clock_1_out));  // open: clr
  Counter #(.width(4), .max('hf)) u_SC (
    .count(INC_SC), .Q(SC), .clk(clock_1_out), .clr(d_ff_1_q));  // open: load, D, carry
  RAM #(.addrWidth(7), .dataWidth(16), .bus("separate")) ram_1 (
    .addr(AR_q), .din(multiplexer_1_out), .data(ram_1_data), .str(MEMORY_WRITE), .clk(clock_1_out),
    .ld(MEMORY_READ));  // open: sel, clr
  assign bit_extender_2_out = {{9{1'b0}}, AR_q};  // Bit_Extender bit_extender_2
  ALU alu_1 (.A(DR_q), .B(AC), .in_3(ALU_SELECTION), .E(out_1), .AC_Output(alu_1_ac_output));
  Multiplexer #(.select(3), .width(16)) multiplexer_1 (
    .in0(ram_1_data), .in1(bit_extender_2_out), .in2(TR_q), .in3(DR_q), .in4(AC), .in5(PC_q),
    .in6({I, OPCode, Address}), .out(multiplexer_1_out), .sel(BUS_SELECTION));  // open: in7, en
endmodule

module ALU (
  input  [15:0] A,
  input  [15:0] B,
  input  [2:0] in_3,
  output E,
  output [15:0] AC_Output
);

  wire adder_1_cout, adder_2_cout, subtractor_1_bout;
  wire [15:0] adder_1_out, adder_2_out, and_1_out, or_1_out, subtractor_1_out, xor_1_out;

  Adder #(.width(16)) adder_1 (.a(A), .b(B), .out(adder_1_out), .cin(1'b0), .cout(adder_1_cout));
  Subtractor #(.width(16)) subtractor_1 (.a(A), .b(B), .out(subtractor_1_out), .bin(1'b0), .bout(subtractor_1_bout));
  assign and_1_out = A & B;  // AND_Gate and_1, 16 bits wide
  assign or_1_out = A | B;  // OR_Gate or_1, 16 bits wide
  assign xor_1_out = A ^ B;  // XOR_Gate xor_1, 16 bits wide
  Adder #(.width(16)) adder_2 (.a(A), .b({16{1'b0}}), .out(adder_2_out), .cin(1'b1), .cout(adder_2_cout));
  or or_2 (E, adder_1_cout, subtractor_1_bout, adder_2_cout);
  Multiplexer #(.select(3), .width(16)) multiplexer_1 (
    .in1(adder_1_out), .in2(subtractor_1_out), .in3(A), .in4(and_1_out), .in5(or_1_out), .in6(xor_1_out),
    .in7(adder_2_out), .out(AC_Output), .sel(in_3));  // open: in0, en
endmodule

module Control_Unit (
  input  I_bit,
  input  [2:0] OPCode,
  input  [3:0] SC,
  input  [11:0] Address_part,
  input  [15:0] AC,
  output LD_AR,
  output LD_PC,
  output LD_DR,
  output LD_IR,
  output memory_write,
  output LD_AC,
  output memory_read,
  output [2:0] Bus_selection,
  output INC_PC,
  output [2:0] ALU_Selection,
  output CLEAR_SC,
  output INC_SC
);

  wire AC_t, and_1_out, and_2_out, and_3_out, and_4_out, and_6_out, and_7_out, and_8_out, and_9_out,
       and_10_out, and_11_out, and_12_out, and_13_out, and_14_out, and_15_out, and_16_out, and_17_out,
       and_18_out, and_19_out, and_20_out, and_21_out, and_22_out, and_23_out, and_24_out, and_25_out,
       and_26_out, and_27_out, and_28_out, and_30_out, and_31_out, and_32_out, and_33_out, and_34_out,
       and_36_out, and_37_out, and_38_out, and_39_out, and_40_out, and_41_out, and_42_out, D0, D1, D2, D3,
       D4, D5, D6, D7, or_3_out, or_7_out, or_10_out, r, T0, T2, T3, T4, T5, T6, T7, T8, T9, T10, T11, T12,
       T13, T14, T15;

  Decoder #(.select(3)) decoder_1 (
    .out0(D0), .out1(D1), .out2(D2), .out3(D3), .out4(D4), .out5(D5), .out6(D6), .out7(D7), .sel(OPCode));  // open: en
  and and_1 (and_1_out, r, Address_part[2], ~AC_t);  // AND_Gate
  and and_2 (and_2_out, D5, T6);
  and and_3 (and_3_out, D2, T5);
  and and_4 (and_4_out, D5, T5);
  Decoder #(.select(4)) decoder_2 (
    .out0(T0), .out1(LD_IR), .out2(T2), .out3(T3), .out4(T4), .out5(T5), .out6(T6), .out7(T7), .out8(T8),
    .out9(T9), .out10(T10), .out11(T11), .out12(T12), .out13(T13), .out14(T14), .out15(T15), .sel(SC));  // open: en
  and and_5 (r, D7, T3, ~I_bit);  // AND_Gate
  or or_1 (AC_t, AC[0], AC[1], AC[2], AC[3], AC[4], AC[5], AC[6], AC[7], AC[8], AC[9], AC[10], AC[11], AC[12], AC[13], AC[14], AC[15]);
  or or_2 (INC_PC, and_1_out, LD_IR);
  and and_6 (and_6_out, D1, T5);
  or or_3 (or_3_out, and_3_out, and_4_out);
  and and_7 (and_7_out, D0, T4);
  and and_8 (and_8_out, D1, T4);
  and and_9 (and_9_out, D2, T4);
  and and_10 (and_10_out, D5, T4);
  and and_11 (and_11_out, D0, T5);
  and and_12 (and_12_out, D0, T4);
  and and_13 (and_13_out, D1, T4);
  and and_14 (and_14_out, D2, T4);
  and and_15 (and_15_out, D5, T4);
  and and_16 (and_16_out, T4, D7, Address_part[5], ~I_bit);  // AND_Gate
  and and_17 (and_17_out, D0, T5);
  and and_18 (and_18_out, D1, T5);
  and and_19 (and_19_out, D2, T5);
  and and_20 (and_20_out, D3, T4);
  and and_21 (and_21_out, D4, T4);
  and and_22 (and_22_out, D5, T6);
  and and_23 (and_23_out, T4, D7, Address_part[5], ~I_bit);  // AND_Gate
  or or_4 (LD_AR, T0, T2);
  and and_24 (and_24_out, D4, T4);
  and and_25 (and_25_out, D3, T4);
  and and_26 (and_26_out, D5, T5);
  and and_27 (and_27_out, r, Address_part[5]);
  and and_28 (and_28_out, r, Address_part[2]);
  and and_29 (LD_PC, D4, T4);
  or or_5 (LD_DR, and_42_out, and_12_out, and_13_out, and_14_out, and_15_out, and_30_out);
  and and_30 (and_30_out, D5, T5);
  or or_6 (memory_read, and_7_out, and_8_out, and_9_out, and_10_out, LD_IR);
  and and_31 (and_31_out, D0, T4);
  and and_32 (and_32_out, D1, T4);
  and and_33 (and_33_out, D2, T4);
  and and_34 (and_34_out, D5, T4);
  or or_7 (or_7_out, and_25_out, and_26_out, and_27_out);
  and and_35 (memory_write, D3, T4);
  and and_36 (and_36_out, D0, T5);
  and and_37 (and_37_out, D2, T5);
  and and_38 (and_38_out, D1, T5);
  and and_39 (and_39_out, D5, T5);
  and and_40 (and_40_out, D5, T6);
  and and_41 (and_41_out, T4, D7, Address_part[5], ~I_bit);  // AND_Gate
  or or_8 (CLEAR_SC, and_17_out, and_18_out, and_19_out, and_20_out, and_21_out, and_22_out, and_28_out, and_23_out);
  and and_42 (and_42_out, r, Address_part[5]);
  Priority_Encoder priority_encoder_1 (
    .in0(1'b0), .in1(and_6_out), .in2(and_2_out), .in3(or_3_out), .in4(and_11_out), .in5(1'b0), .in6(1'b0),
    .in7(and_16_out), .out(ALU_Selection));  // open: en_in, gs, en_out
  not not_1 (INC_SC, CLEAR_SC);
  or or_9 (LD_AC, and_36_out, and_37_out, and_38_out, and_39_out, and_40_out, and_41_out);
  or or_10 (or_10_out, and_31_out, and_32_out, and_33_out, and_34_out, LD_IR);
  Priority_Encoder priority_encoder_2 (
    .in0(or_10_out), .in1(and_24_out), .in2(1'b0), .in3(1'b0), .in4(or_7_out), .in5(T0), .in6(T2),
    .in7(1'b0), .out(Bus_selection));  // open: en_in, gs, en_out

  // Other names for the same wires on the sheet: B0 = Address_part[0]; B1 = Address_part[1]; B2 = Address_part[2];
  //   B3 = Address_part[3]; B4 = Address_part[4]; B5 = Address_part[5]; B6 = Address_part[6]; B7 = Address_part[7];
  //   B8 = Address_part[8]; B9 = Address_part[9]; B10 = Address_part[10]; B11 = Address_part[11]; I = I_bit;
  //   T1 = LD_IR
endmodule
